// Digital circuit Computer.dig as structural Verilog
module Computer (
);

  wire undriven, undriven_2, undriven_3, undriven_4, undriven_5, undriven_6, undriven_7, undriven_8;

  Control_Logic control_logic_1 ();  // open: CF, ZF, IR__4, IR__5, IR__6, IR__7, CLK__hat, CLR__hat, CLR, HLT, MI__hat, RI, RO__hat, IO__hat, II__hat, AI__hat, AO__hat, EO__hat, SU, BI__hat, OI, CE, CO__hat, J__hat, FI__hat
  Random_Access_Memory random_access_memory_1 ();
  Instruction_Register instruction_register_1 ();  // open: BUS__0, BUS__1, BUS__2, BUS__3, BUS__4, BUS__5, BUS__6, BUS__7, I1__hat, CLR, I0__hat, CLK, IR__4, IR__5, IR__6, IR__7
  Clock clock_1 ();  // open: U1, HLT, CLK__hat, CLK
  Memory_Address_Register memory_address_register_1 ();
  LED BUS__7 (.in(undriven));
  LED BUS__6 (.in(undriven_2));
  LED BUS__5 (.in(undriven_3));
  LED BUS__4 (.in(undriven_4));
  LED BUS__3 (.in(undriven_5));
  LED BUS__2 (.in(undriven_6));
  LED BUS__1 (.in(undriven_7));
  LED BUS__0 (.in(undriven_8));
  Arithmetic_Logic_Unit arithmetic_logic_unit_1 ();  // open: FI__hat, CLK, CLR, A__7, A__6, A__5, A__4, A__3, A__2, A__1, A__0, B__7, B__6, B__5, B__4, B__3, B__2, B__1, B__0, EO__hat, SU, CF, ZF, BUS__0, BUS__1, BUS__2, BUS__3, BUS__4, BUS__5, BUS__6, BUS__7
  Output_Register output_register_1 ();  // open: BUS__0, BUS__1, BUS__2, BUS__3, BUS__4, BUS__5, BUS__6, BUS__7, OI, CLK, CLR__hat, MUX__CLK
  A_Register a_register_1 ();  // open: BUS__0, BUS__1, BUS__2, BUS__3, BUS__4, BUS__5, BUS__6, BUS__7, AI__hat, CLR, AO__hat, CLK, A__0, A__1, A__2, A__3, A__4, A__5, A__6, A__7
  B_Register b_register_1 ();  // open: BUS__0, BUS__1, BUS__2, BUS__3, BUS__4, BUS__5, BUS__6, BUS__7, BI__hat, CLR, BO__hat, CLK, B__0, B__1, B__2, B__3, B__4, B__5, B__6, B__7
  Program_Counter program_counter_1 ();  // open: J__hat, CE, CLK, CLR__hat, CO__hat, BUS__0, BUS__1, BUS__2, BUS__3
endmodule
